// Logisim project cpu.circ as structural Verilog: 5 circuits, main circuit main
// CPU
module main (
  input  [31:0] RS_READ_VALUE,
  input  [31:0] RI_READ_VALUE,
  input  [31:0] RD_READ_VALUE,
  input  [31:0] JC_READ_VALUE,
  input  [31:0] INSTRUCTION,
  input  CLOCK,
  output [4:0] RS,
  output [4:0] RI,
  output [4:0] RD,
  output [31:0] RD_WRITE_VALUE,
  output RD_WRITE_ENABLE,
  output [23:0] FETCH_ADDRESS
);

  wire and_1_out, comparator_1_eq, comparator_2_eq, comparator_3_eq, comparator_4_eq, comparator_5_eq,
       comparator_6_eq, comparator_7_eq, comparator_8_gt, comparator_9_eq, comparator_10_eq,
       comparator_11_eq, comparator_12_eq, comparator_13_eq, comparator_14_eq, comparator_14_gt,
       comparator_15_eq, comparator_16_lt, comparator_17_eq, comparator_17_lt, I, load, mem_write, not_1_out,
       not_2_out, not_3_out, not_4_out, or_3_out, or_5_out, or_6_out, word_mode, ZERO;
  wire [2:0] JC;
  wire [3:0] OP;
  wire [16:0] IMMEDIATE;
  wire [23:0] ADDRESS, bit_extender_4_out, jump, jump_address, multiplexer_2_out, multiplexer_6_out,
       multiplexer_7_out, multiplexer_8_out, multiplexer_9_out, multiplexer_10_out, multiplexer_11_out, next;
  wire [24:0] bit_extender_3_out;
  wire [31:0] bit_extender_1_out, bit_extender_2_out, mem_to_reg, multiplexer_1_out, multiplexer_4_out,
       write_to_reg;

  // Probe on RS
  // Probe on RI
  // Probe on RD
  assign bit_extender_1_out = {{15{IMMEDIATE[16]}}, IMMEDIATE};  // Bit_Extender bit_extender_1
  Register #(.width(24)) PC (.D(multiplexer_2_out), .Q(FETCH_ADDRESS), .clk(CLOCK));  // open: en, clr
  assign bit_extender_2_out = {{8{1'b0}}, next};  // Bit_Extender bit_extender_2
  Multiplexer #(.width(32), .enable("false")) multiplexer_1 (
    .in0(RI_READ_VALUE), .in1(bit_extender_1_out), .out(multiplexer_1_out), .sel(I));
  Bit_Extender #(.in_width(32), .out_width(25)) bit_extender_3 (.in(write_to_reg), .out(bit_extender_3_out));
  Adder #(.width(24)) adder_1 (.a(FETCH_ADDRESS), .b(24'h1), .out(next));  // open: cin, cout
  u_ALU u_alu_1 (
    .ALU_X(RS_READ_VALUE), .ALU_Y(multiplexer_1_out), .ALU_RESULT(write_to_reg), .ALU_CONTROL(OP),
    .NEXT(bit_extender_2_out));
  u_MEM u_mem_1 (
    .ADDRESS(bit_extender_3_out), .WORD_MODE(word_mode), .MEM_WRITE(mem_write), .DATA_IN(RD_READ_VALUE),
    .CLOCK(CLOCK), .DATA_OUT(mem_to_reg));
  u_DEC u_dec_1 (
    .INSTRUCTION(INSTRUCTION), .OP(OP), .JC(JC), .I(I), .RD(RD), .RS(RS), .RI(RI), .IMMEDIATE(IMMEDIATE),
    .ADDRESS(ADDRESS), .ZERO(ZERO));
  Comparator #(.width(4)) comparator_1 (.a(OP), .b(4'b1111), .eq(comparator_1_eq));  // open: gt, lt
  Multiplexer #(.width(24), .enable("false")) multiplexer_2 (
    .in0(next), .in1(jump_address), .out(multiplexer_2_out), .sel(comparator_1_eq));
  // Probe on load
  Comparator #(.width(4)) comparator_2 (.a(OP), .b(4'b1011), .eq(comparator_2_eq));  // open: gt, lt
  or or_1 (mem_write, comparator_2_eq, comparator_3_eq);
  Bit_Extender #(.in_width(32), .out_width(24)) bit_extender_4 (.in(RI_READ_VALUE), .out(bit_extender_4_out));
  Comparator #(.width(4)) comparator_3 (.a(OP), .b(4'b1101), .eq(comparator_3_eq));  // open: gt, lt
  Multiplexer #(.select(3), .width(24), .enable("false")) multiplexer_3 (
    .in0(jump), .in1(multiplexer_6_out), .in2(multiplexer_8_out), .in3(multiplexer_10_out),
    .in4(multiplexer_11_out), .in5(multiplexer_7_out), .in6(multiplexer_9_out), .in7(jump),
    .out(jump_address), .sel(JC));
  Multiplexer #(.width(32), .enable("false")) multiplexer_4 (
    .in0(write_to_reg), .in1(mem_to_reg), .out(multiplexer_4_out), .sel(load));
  Demultiplexer #(.width(32), .enable("false")) demultiplexer_1 (
    .out1(RD_WRITE_VALUE), .in(multiplexer_4_out), .sel(RD_WRITE_ENABLE));  // open: out0
  Multiplexer #(.width(24), .enable("false")) multiplexer_5 (
    .in0(bit_extender_4_out), .in1(ADDRESS), .out(jump), .sel(I));
  Comparator #(.width(4)) comparator_4 (.a(OP), .b(4'b1100), .eq(comparator_4_eq));  // open: gt, lt
  or or_2 (word_mode, comparator_4_eq, comparator_5_eq);
  Comparator #(.width(4)) comparator_5 (.a(OP), .b(4'b1101), .eq(comparator_5_eq));  // open: gt, lt
  Comparator #(.width(4)) comparator_6 (.a(OP), .b(4'b1111), .eq(comparator_6_eq));  // open: gt, lt
  and and_1 (and_1_out, comparator_6_eq, not_4_out);
  Comparator #(.width(4)) comparator_7 (.a(OP), .b(4'b1011), .eq(comparator_7_eq));  // open: gt, lt
  or or_3 (or_3_out, comparator_7_eq, and_1_out, comparator_10_eq);
  not not_1 (not_1_out, or_3_out);
  Comparator #(.width(32)) comparator_8 (.a(JC_READ_VALUE), .b({32{1'b0}}), .gt(comparator_8_gt));  // open: eq, lt
  Multiplexer #(.width(24), .enable("false")) multiplexer_6 (
    .in0(next), .in1(jump), .out(multiplexer_6_out), .sel(comparator_8_gt));
  Comparator #(.width(32)) comparator_9 (.a(JC_READ_VALUE), .b({32{1'b0}}), .eq(comparator_9_eq));  // open: gt, lt
  Comparator #(.width(4)) comparator_10 (.a(OP), .b(4'b1101), .eq(comparator_10_eq));  // open: gt, lt
  not not_2 (not_2_out, ZERO);
  not not_3 (not_3_out, comparator_9_eq);
  Multiplexer #(.width(24), .enable("false")) multiplexer_7 (
    .in0(next), .in1(jump), .out(multiplexer_7_out), .sel(not_3_out));
  Comparator #(.width(3)) comparator_11 (.a(JC), .b(3'b111), .eq(comparator_11_eq));  // open: gt, lt
  and and_2 (RD_WRITE_ENABLE, not_2_out, not_1_out);
  not not_4 (not_4_out, comparator_11_eq);
  Comparator #(.width(4)) comparator_12 (.a(OP), .b(4'b1010), .eq(comparator_12_eq));  // open: gt, lt
  or or_4 (load, comparator_12_eq, comparator_15_eq);
  Comparator #(.width(32)) comparator_13 (.a(JC_READ_VALUE), .b({32{1'b0}}), .eq(comparator_13_eq));  // open: gt, lt
  Multiplexer #(.width(24), .enable("false")) multiplexer_8 (
    .in0(next), .in1(jump), .out(multiplexer_8_out), .sel(comparator_13_eq));
  Comparator #(.width(32)) comparator_14 (
    .a(JC_READ_VALUE), .b({32{1'b0}}), .gt(comparator_14_gt), .eq(comparator_14_eq));  // open: lt
  Comparator #(.width(4)) comparator_15 (.a(OP), .b(4'b1100), .eq(comparator_15_eq));  // open: gt, lt
  or or_5 (or_5_out, comparator_14_eq, comparator_14_gt);
  Multiplexer #(.width(24), .enable("false")) multiplexer_9 (
    .in0(next), .in1(jump), .out(multiplexer_9_out), .sel(or_5_out));
  Comparator #(.width(32)) comparator_16 (.a(JC_READ_VALUE), .b({32{1'b0}}), .lt(comparator_16_lt));  // open: gt, eq
  Multiplexer #(.width(24), .enable("false")) multiplexer_10 (
    .in0(next), .in1(jump), .out(multiplexer_10_out), .sel(comparator_16_lt));
  Comparator #(.width(32)) comparator_17 (
    .a(JC_READ_VALUE), .b({32{1'b0}}), .eq(comparator_17_eq), .lt(comparator_17_lt));  // open: gt
  or or_6 (or_6_out, comparator_17_eq, comparator_17_lt);
  Multiplexer #(.width(24), .enable("false")) multiplexer_11 (
    .in0(next), .in1(jump), .out(multiplexer_11_out), .sel(or_6_out));

  // Notes on the sheet:
  //   Register Write Control
  //   Jump Address Control
endmodule

module u_ALU (
  input  [31:0] ALU_X,
  input  [31:0] NEXT,
  input  [31:0] ALU_Y,
  input  [3:0] ALU_CONTROL,
  output [31:0] ALU_RESULT
);

  wire and_2_out, bit_extender_4_out, comparator_1_eq, comparator_2_eq, comparator_2_lt, xor_4_out;
  wire [4:0] bit_extender_1_out, bit_extender_2_out, bit_extender_3_out, subtractor_1_out;
  wire [31:0] _00, _01, _02, _03, _04, _05, _06, _07, _08, _09, _10, _11, _12, _13, _14, adder_4_out,
       adder_5_out, adder_8_out, divider_1_out, multiplexer_3_out, multiplexer_4_out, multiplexer_5_out,
       multiplexer_6_out, multiplexer_8_out, or_1_out, shifter_1_out, shifter_2_out, xor_2_out, xor_3_out,
       xor_5_out;

  Bit_Extender #(.in_width(32), .out_width(5)) bit_extender_1 (.in(ALU_Y), .out(bit_extender_1_out));
  Bit_Extender #(.in_width(32), .out_width(5)) bit_extender_2 (.in(ALU_Y), .out(bit_extender_2_out));
  Bit_Extender #(.in_width(32), .out_width(5)) bit_extender_3 (.in(ALU_Y), .out(bit_extender_3_out));
  Bit_Extender #(.in_width(32), .out_width(1)) bit_extender_4 (.in(ALU_X), .out(bit_extender_4_out));
  Shifter #(.width(32)) shifter_1 (.in(ALU_X), .\dist (bit_extender_1_out), .out(shifter_1_out));
  assign or_1_out = shifter_1_out | shifter_2_out;  // OR_Gate or_1, 32 bits wide
  Shifter #(.width(32), .shift("lr")) shifter_2 (.in({32{1'b1}}), .\dist (subtractor_1_out), .out(shifter_2_out));
  Subtractor #(.width(5)) subtractor_1 (
    .a({5{1'b1}}), .b(bit_extender_1_out), .out(subtractor_1_out));  // open: bin, bout
  Shifter #(.width(32), .shift("ar")) shifter_3 (.in(ALU_X), .\dist (bit_extender_2_out), .out(_01));
  assign _02 = ALU_X & ALU_Y;  // AND_Gate and_1, 32 bits wide
  assign _03 = ALU_X | ALU_Y;  // OR_Gate or_2, 32 bits wide
  u_REV u_rev_1 (.INPUT(ALU_X), .REVERSE_AMOUNT(bit_extender_3_out), .OUTPUT(_04));
  assign _05 = ALU_X ^ ALU_Y;  // XOR_Gate xor_1, 32 bits wide
  Adder #(.width(32)) adder_1 (.a(ALU_X), .b(ALU_Y), .out(_06));  // open: cin, cout
  Subtractor #(.width(32)) subtractor_2 (.a(ALU_X), .b(ALU_Y), .out(_07));  // open: bin, bout
  Multiplexer #(.width(32), .enable("false")) multiplexer_1 (
    .in0(shifter_1_out), .in1(or_1_out), .out(_00), .sel(bit_extender_4_out));
  Multiplier #(.width(32)) multiplier_1 (.a(ALU_X), .b(ALU_Y), .out(_08));  // open: cin, cout
  Bit_Extender #(.in_width(32), .out_width(15)) bit_extender_5 (.in(ALU_X), .out(_14[14:0]));
  Bit_Extender #(.in_width(32), .out_width(17)) bit_extender_6 (.in(ALU_Y), .out(_14[31:15]));
  Comparator #(.width(32)) comparator_1 (.a(ALU_Y), .b({32{1'b0}}), .eq(comparator_1_eq));  // open: gt, lt
  Multiplexer #(.select(4), .width(32), .enable("false")) multiplexer_2 (
    .in0(_00), .in1(_01), .in2(_02), .in3(_03), .in4(_04), .in5(_05), .in6(_06), .in7(_07), .in8(_08),
    .in9(_09), .in10(_10), .in11(_11), .in12(_12), .in13(_13), .in14(_14), .in15(NEXT), .out(ALU_RESULT),
    .sel(ALU_CONTROL));
  Adder #(.width(32)) adder_2 (.a(ALU_X), .b(ALU_Y), .out(_10));  // open: cin, cout
  Multiplexer #(.width(32), .enable("false")) multiplexer_3 (
    .in0(multiplexer_8_out), .in1(multiplexer_6_out), .out(multiplexer_3_out), .sel(comparator_1_eq));
  assign xor_2_out = ALU_X ^ {32{1'b1}};  // XOR_Gate xor_2, 32 bits wide
  assign xor_3_out = ALU_Y ^ {32{1'b1}};  // XOR_Gate xor_3, 32 bits wide
  Adder #(.width(32)) adder_3 (.a(ALU_X), .b(ALU_Y), .out(_11));  // open: cin, cout
  Adder #(.width(32)) adder_4 (.a(xor_2_out), .b(32'h1), .out(adder_4_out));  // open: cin, cout
  Adder #(.width(32)) adder_5 (.a(xor_3_out), .b(32'h1), .out(adder_5_out));  // open: cin, cout
  Adder #(.width(32)) adder_6 (.a(ALU_X), .b(ALU_Y), .out(_12));  // open: cin, cout
  Comparator #(.width(32)) comparator_2 (
    .a(ALU_X), .b({32{1'b0}}), .eq(comparator_2_eq), .lt(comparator_2_lt));  // open: gt
  Multiplexer #(.width(32), .enable("false")) multiplexer_4 (
    .in0(ALU_X), .in1(adder_4_out), .out(multiplexer_4_out), .sel(ALU_X[31]));
  Multiplexer #(.width(32), .enable("false")) multiplexer_5 (
    .in0(ALU_Y), .in1(adder_5_out), .out(multiplexer_5_out), .sel(ALU_Y[31]));
  Adder #(.width(32)) adder_7 (.a(ALU_X), .b(ALU_Y), .out(_13));  // open: cin, cout
  Multiplexer #(.width(32), .enable("false")) multiplexer_6 (
    .in0(32'h7fffffff), .in1(32'h80000000), .out(multiplexer_6_out), .sel(comparator_2_lt));
  and and_2 (and_2_out, comparator_2_eq, comparator_1_eq);
  Divider #(.width(32)) divider_1 (
    .a(multiplexer_4_out), .b(multiplexer_5_out), .out(divider_1_out));  // open: upper, rem
  xor xor_4 (xor_4_out, ALU_X[31], ALU_Y[31]);
  Multiplexer #(.width(32), .enable("false")) multiplexer_7 (
    .in0(multiplexer_3_out), .in1({32{1'b0}}), .out(_09), .sel(and_2_out));
  Multiplexer #(.width(32), .enable("false")) multiplexer_8 (
    .in0(divider_1_out), .in1(adder_8_out), .out(multiplexer_8_out), .sel(xor_4_out));
  assign xor_5_out = divider_1_out ^ {32{1'b1}};  // XOR_Gate xor_5, 32 bits wide
  Adder #(.width(32)) adder_8 (.a(xor_5_out), .b(32'h1), .out(adder_8_out));  // open: cin, cout

  // Other names for the same wires on the sheet: _15[31:0] = NEXT; result[31:0] = ALU_RESULT; x[31:0] = ALU_X;
  //   y[31:0] = ALU_Y

  // Notes on the sheet:
  //   Signed Division
endmodule

// Data Memory
module u_MEM (
  input  [24:0] ADDRESS,
  input  WORD_MODE,
  input  MEM_WRITE,
  input  [31:0] DATA_IN,
  input  CLOCK,
  output [31:0] DATA_OUT
);

  wire and_1_out, and_2_out, not_1_out, or_1_out, or_2_out;
  wire [15:0] eout, multiplexer_2_out, multiplexer_3_out, multiplexer_4_out, multiplexer_5_out, oout;
  wire [23:0] adder_1_out, multiplexer_1_out;
  wire [31:0] bit_extender_1_out;

  // Probe on DATA_IN[15:0]
  // Probe on DATA_IN[31:16]
  Adder #(.width(24)) adder_1 (.a(ADDRESS[24:1]), .b(24'h1), .out(adder_1_out));  // open: cin, cout
  not not_1 (not_1_out, ADDRESS[0]);
  Multiplexer #(.width(24), .enable("false")) multiplexer_1 (
    .in0(ADDRESS[24:1]), .in1(adder_1_out), .out(multiplexer_1_out), .sel(ADDRESS[0]));
  Multiplexer #(.width(16), .enable("false")) multiplexer_2 (
    .in0(DATA_IN[15:0]), .in1(DATA_IN[31:16]), .out(multiplexer_2_out), .sel(ADDRESS[0]));
  and and_1 (and_1_out, MEM_WRITE, or_1_out);
  or or_1 (or_1_out, not_1_out, WORD_MODE);
  RAM #(.addrWidth(24), .dataWidth(16), .bus("separate")) ram_1 (
    .addr(multiplexer_1_out), .din(multiplexer_2_out), .data(eout), .str(and_1_out), .clk(CLOCK));  // open: sel, ld, clr
  Multiplexer #(.width(16), .enable("false")) multiplexer_3 (
    .in0(DATA_IN[31:16]), .in1(DATA_IN[15:0]), .out(multiplexer_3_out), .sel(ADDRESS[0]));
  and and_2 (and_2_out, MEM_WRITE, or_2_out);
  or or_2 (or_2_out, ADDRESS[0], WORD_MODE);
  Multiplexer #(.width(16), .enable("false")) multiplexer_4 (
    .in0(eout), .in1(oout), .out(multiplexer_4_out), .sel(ADDRESS[0]));
  Multiplexer #(.width(16), .enable("false")) multiplexer_5 (
    .in0(oout), .in1(eout), .out(multiplexer_5_out), .sel(ADDRESS[0]));
  assign bit_extender_1_out = {{16{multiplexer_4_out[15]}}, multiplexer_4_out};  // Bit_Extender bit_extender_1
  // Probe on multiplexer_4_out
  // Probe on multiplexer_5_out
  RAM #(.addrWidth(24), .dataWidth(16), .bus("separate")) ram_2 (
    .addr(ADDRESS[24:1]), .din(multiplexer_3_out), .data(oout), .str(and_2_out), .clk(CLOCK));  // open: sel, ld, clr
  Multiplexer #(.width(32), .enable("false")) multiplexer_6 (
    .in0(bit_extender_1_out), .in1({multiplexer_5_out, multiplexer_4_out}), .out(DATA_OUT), .sel(WORD_MODE));
  // Probe on DATA_OUT

  // Other names for the same wires on the sheet: o = ADDRESS[0]; even[23:0] = ADDRESS[24:1];
  //   odd[23:0] = ADDRESS[24:1]; c = CLOCK; din[15:0] = DATA_IN[15:0]; din2[15:0] = DATA_IN[31:16]; m = WORD_MODE;
  //   s = MEM_WRITE

  // Notes on the sheet:
  //   Feel free to use this component, or not, however you want!
  //   You might use the word mode input to differentiate LW/SW from LH/SH.
  //   However, you *SHOULD* use 2 RAM modules, one for even addresses and one for odd addresses.
endmodule

module u_REV (
  input  [31:0] INPUT,
  input  [4:0] REVERSE_AMOUNT,
  output [31:0] OUTPUT
);

  wire [31:0] _2in, _3in, _4in, _5in;

  Multiplexer #(.width(32), .enable("false")) multiplexer_1 (
    .in0(INPUT),
    .in1({INPUT[30], INPUT[31], INPUT[28], INPUT[29], INPUT[26], INPUT[27], INPUT[24], INPUT[25], INPUT[22], INPUT[23], INPUT[20], INPUT[21], INPUT[18], INPUT[19], INPUT[16], INPUT[17], INPUT[14], INPUT[15], INPUT[12], INPUT[13], INPUT[10], INPUT[11], INPUT[8], INPUT[9], INPUT[6], INPUT[7], INPUT[4], INPUT[5], INPUT[2], INPUT[3], INPUT[0], INPUT[1]}),
    .out(_2in), .sel(REVERSE_AMOUNT[0]));
  Multiplexer #(.width(32), .enable("false")) multiplexer_2 (
    .in0(_2in),
    .in1({_2in[29:28], _2in[31:30], _2in[25:24], _2in[27:26], _2in[21:20], _2in[23:22], _2in[17:16], _2in[19:18], _2in[13:12], _2in[15:14], _2in[9:8], _2in[11:10], _2in[5:4], _2in[7:6], _2in[1:0], _2in[3:2]}),
    .out(_3in), .sel(REVERSE_AMOUNT[1]));
  Multiplexer #(.width(32), .enable("false")) multiplexer_3 (
    .in0(_3in),
    .in1({_3in[27:24], _3in[31:28], _3in[19:16], _3in[23:20], _3in[11:8], _3in[15:12], _3in[3:0], _3in[7:4]}),
    .out(_4in), .sel(REVERSE_AMOUNT[2]));
  Multiplexer #(.width(32), .enable("false")) multiplexer_4 (
    .in0(_4in), .in1({_4in[23:16], _4in[31:24], _4in[7:0], _4in[15:8]}), .out(_5in), .sel(REVERSE_AMOUNT[3]));
  Multiplexer #(.width(32), .enable("false")) multiplexer_5 (
    .in0(_5in), .in1({_5in[15:0], _5in[31:16]}), .out(OUTPUT), .sel(REVERSE_AMOUNT[4]));

  // Other names for the same wires on the sheet: _1in[31:0] = INPUT;
  //   _1out[31:0] = {INPUT[30], INPUT[31], INPUT[28], INPUT[29], INPUT[26], INPUT[27], INPUT[24], INPUT[25], INPUT[22], INPUT[23], INPUT[20], INPUT[21], INPUT[18], INPUT[19], INPUT[16], INPUT[17], INPUT[14], INPUT[15], INPUT[12], INPUT[13], INPUT[10], INPUT[11], INPUT[8], INPUT[9], INPUT[6], INPUT[7], INPUT[4], INPUT[5], INPUT[2], INPUT[3], INPUT[0], INPUT[1]};
  //   _2out[31:0] = {_2in[29:28], _2in[31:30], _2in[25:24], _2in[27:26], _2in[21:20], _2in[23:22], _2in[17:16], _2in[19:18], _2in[13:12], _2in[15:14], _2in[9:8], _2in[11:10], _2in[5:4], _2in[7:6], _2in[1:0], _2in[3:2]};
  //   _3out[31:0] = {_3in[27:24], _3in[31:28], _3in[19:16], _3in[23:20], _3in[11:8], _3in[15:12], _3in[3:0], _3in[7:4]};
  //   _4out[31:0] = {_4in[23:16], _4in[31:24], _4in[7:0], _4in[15:8]}; _5out[31:0] = {_5in[15:0], _5in[31:16]};
  //   result[31:0] = OUTPUT

  // Notes on the sheet:
  //   Feel free to use this component, or not, however you want!
endmodule

module u_DEC (
  input  [31:0] INSTRUCTION,
  output ZERO,
  output [3:0] OP,
  output [2:0] JC,
  output I,
  output [4:0] RD,
  output [4:0] RS,
  output [4:0] RI,
  output [16:0] IMMEDIATE,
  output [23:0] ADDRESS
);

  wire and_1_out, comparator_2_eq, comparator_3_eq;
  wire [16:0] demultiplexer_1_out0;
  wire [23:0] demultiplexer_2_out0;

  Demultiplexer #(.width(17), .enable("false")) demultiplexer_1 (
    .out0(demultiplexer_1_out0), .out1(IMMEDIATE), .in(INSTRUCTION[16:0]), .sel(INSTRUCTION[27]));
  Demultiplexer #(.width(24), .enable("false")) demultiplexer_2 (
    .out0(demultiplexer_2_out0), .out1(ADDRESS), .in(INSTRUCTION[23:0]), .sel(INSTRUCTION[27]));
  Comparator #(.width(32)) comparator_1 (.a(INSTRUCTION), .b({32{1'b0}}), .eq(ZERO));  // open: gt, lt
  Comparator #(.width(4)) comparator_2 (.a(INSTRUCTION[31:28]), .b(4'b1111), .eq(comparator_2_eq));  // open: gt, lt
  Multiplexer #(.width(5), .enable("false")) multiplexer_1 (
    .in0(demultiplexer_1_out0[4:0]), .in1(demultiplexer_2_out0[4:0]), .out(RI), .sel(comparator_2_eq));
  and and_1 (and_1_out, comparator_2_eq, comparator_3_eq);
  Comparator #(.width(3)) comparator_3 (.a(INSTRUCTION[26:24]), .b(3'b111), .eq(comparator_3_eq));  // open: gt, lt
  Multiplexer #(.width(5), .enable("false")) multiplexer_2 (
    .in0(INSTRUCTION[26:22]), .in1(5'b00110), .out(RD), .sel(and_1_out));

  assign I = INSTRUCTION[27];
  assign JC = INSTRUCTION[26:24];
  assign OP = INSTRUCTION[31:28];
  assign RS = INSTRUCTION[21:17];

  // Other names for the same wires on the sheet: J_TYPE[26:0] = INSTRUCTION[26:0]; R_TYPE[26:0] = INSTRUCTION[26:0];
  //   RD_T[4:0] = INSTRUCTION[26:22]
endmodule
